# Fritzing sketch sketch (saved by Fritzing 0.9.2b)
circuit board: 8.46667cm x 5.64444cm
breadboards: 1

parts:
  RHT1 = Humidity and Temperature Sensor RHT03
  S1 = Pushbutton [package="[SMD]"]
  R1 = Resistor [tolerance=±5% resistance=220 package=THT]
  U2 = BATTERY-2 [package=battery-aaa]
  U4 = Voltage Regulator - 3.3V [package="TO220 [THT]"]
  IC1 = esp8266 [package=THT]

nets:
  N1: RHT1.Vcc, R1.Pin_1, U4.output_voltage, IC1.CHIPD, IC1.+V
  N2: RHT1.Data-signal, R1.Pin_0, IC1.GPIO2
  GND: RHT1.GND_2, S1.Pin_3, S1.Pin_4, U2.-2, U4.GND, IC1.GND
  N3: S1.Pin_1, S1.Pin_2, IC1.GPIO0
  N4: U2.-1, U4.input_voltage

custom parts:
  Voltage Regulator - 3.3V: 3.3V DC Voltage Regulator
